# Fritzing sketch Fritzing Diagram (saved by Fritzing 0.9.3b)
breadboards: 1

parts:
  Part1 = Photon
  HC-SR04_Sensor_1 = HC-SR04 Ultrasonic Distance Sensor
  3-Axis_Accelerometer1 = 3-Axis Accelerometer Breakout - MMA8452Q
  SG1 = Buzzer 12mm [package=buzzer-12mm]

nets:
  N1: Part1.A0, HC-SR04_Sensor_1.TRIG
  GND: Part1.GND, HC-SR04_Sensor_1.GND, 3-Axis_Accelerometer1.GND, SG1.2
  VIN: Part1.VIN, HC-SR04_Sensor_1.VCC
  N2: Part1.D0, 3-Axis_Accelerometer1.SDA
  N3: Part1.D1, 3-Axis_Accelerometer1.SCL
  N4: Part1.D5, HC-SR04_Sensor_1.ECHO
  N5: Part1.D6, SG1.1
  3V3: Part1.3V3, 3-Axis_Accelerometer1.3.3V
